// Logisim project CPU.circ as structural Verilog: 2 circuits, main circuit main
module main (
  input  in_1
);

  wire and_1_out, and_2_out, and_3_out, and_4_out, and_5_out, and_6_out, clock_1_out, decoder_1_out0,
       decoder_1_out1, decoder_1_out2, decoder_1_out3, decoder_2_out0, decoder_2_out1, decoder_2_out2,
       decoder_2_out3, decoder_3_out0, not_1_out, not_2_out, not_3_out, not_4_out, not_5_out, not_6_out,
       or_1_out;
  wire [3:0] controlled_buffer_1_out, counter_2_q, register_1_q, register_2_q;
  wire [7:0] counter_1_q, rom_1_data;
  wire [7:4] controlled_buffer_1_out_2;

  Clock clock_1 (.out(clock_1_out));
  Counter counter_1 (.Q(counter_1_q), .clk(clock_1_out), .clr(in_1));  // open: load, D, count, carry
  Counter #(.width(4), .max('hf)) counter_2 (
    .Q(counter_2_q), .clk(clock_1_out), .clr(or_1_out));  // open: load, D, count, carry
  or or_1 (or_1_out, in_1, decoder_2_out3);
  Register #(.width(4)) register_1 (
    .D(controlled_buffer_1_out), .Q(register_1_q), .clk(not_1_out), .clr(in_1));  // open: en
  Decoder #(.select(4)) decoder_1 (
    .out0(decoder_1_out0), .out1(decoder_1_out1), .out2(decoder_1_out2), .out3(decoder_1_out3),
    .sel(register_1_q));  // open: out4, out5, out6, out7, out8, out9, out10, out11, out12, out13, out14, out15, en
  Decoder #(.select(4)) decoder_2 (
    .out0(decoder_2_out0), .out1(decoder_2_out1), .out2(decoder_2_out2), .out3(decoder_2_out3),
    .sel(counter_2_q));  // open: out4, out5, out6, out7, out8, out9, out10, out11, out12, out13, out14, out15, en
  ROM rom_1 (.addr(counter_1_q), .data(rom_1_data));  // open: sel
  assign {controlled_buffer_1_out_2, controlled_buffer_1_out} = decoder_3_out0 ? rom_1_data : 8'bz;  // Controlled_Buffer controlled_buffer_1
  not not_1 (not_1_out, and_1_out);
  Register #(.width(4)) register_2 (.D(rom_1_data[3:0]), .Q(register_2_q), .clk(not_2_out), .clr(in_1));  // open: en
  not not_2 (not_2_out, decoder_2_out0);
  and and_1 (and_1_out, decoder_3_out0, decoder_2_out1);
  Register register_3 (
    .D({controlled_buffer_1_out_2, controlled_buffer_1_out}), .clk(and_2_out), .clr(in_1));  // open: en, Q
  and and_2 (and_2_out, decoder_1_out0, not_3_out);
  not not_3 (not_3_out, and_6_out);
  Register register_4 (
    .D({controlled_buffer_1_out_2, controlled_buffer_1_out}), .clk(and_3_out), .clr(in_1));  // open: en, Q
  and and_3 (and_3_out, decoder_1_out1, not_4_out);
  not not_4 (not_4_out, and_6_out);
  Register register_5 (
    .D({controlled_buffer_1_out_2, controlled_buffer_1_out}), .clk(and_4_out), .clr(in_1));  // open: en, Q
  and and_4 (and_4_out, decoder_1_out2, not_5_out);
  not not_5 (not_5_out, and_6_out);
  Register register_6 (
    .D({controlled_buffer_1_out_2, controlled_buffer_1_out}), .clk(and_5_out), .clr(in_1));  // open: en, Q
  and and_5 (and_5_out, decoder_1_out3, not_6_out);
  not not_6 (not_6_out, and_6_out);
  Decoder #(.select(4)) decoder_3 (
    .out0(decoder_3_out0), .sel(register_2_q));  // open: out1, out2, out3, out4, out5, out6, out7, out8, out9, out10, out11, out12, out13, out14, out15, en
  and and_6 (and_6_out, decoder_2_out2, decoder_3_out0);

  // Notes on the sheet:
  //   contents of rom_1 (hex, n*v repeats v):
  //   0 0 1 0 1 22 0 2 17 0 3 ff
endmodule

module ALU_8bit (
  input  O0,
  input  O1,
  input  A0,
  input  O2,
  input  A1,
  input  O3,
  input  A2,
  input  A3,
  input  A4,
  input  A5,
  input  A6,
  input  A7,
  input  B0,
  input  B1,
  input  B2,
  input  B3,
  input  B4,
  input  B5,
  input  B6,
  input  B7,
  output C0,
  output C1,
  output C2,
  output C3,
  output C4,
  output C5,
  output C6,
  output C7
);

  wire [7:0] adder_1_out, and_1_out, divider_1_out, multiplier_1_out, nand_1_out, nor_1_out, not_1_out,
       or_1_out, subtractor_1_out, xor_1_out;

  assign and_1_out = {A7, A6, A5, A4, A3, A2, A1, A0} & {B7, B6, B5, B4, B3, B2, B1, B0};  // AND_Gate and_1, 8 bits wide
  assign or_1_out = {A7, A6, A5, A4, A3, A2, A1, A0} | {B7, B6, B5, B4, B3, B2, B1, B0};  // OR_Gate or_1, 8 bits wide
  assign xor_1_out = {A7, A6, A5, A4, A3, A2, A1, A0} ^ {B7, B6, B5, B4, B3, B2, B1, B0};  // XOR_Gate xor_1, 8 bits wide
  assign nand_1_out = ~({A7, A6, A5, A4, A3, A2, A1, A0} & {B7, B6, B5, B4, B3, B2, B1, B0});  // NAND_Gate nand_1, 8 bits wide
  assign nor_1_out = ~({A7, A6, A5, A4, A3, A2, A1, A0} | {B7, B6, B5, B4, B3, B2, B1, B0});  // NOR_Gate nor_1, 8 bits wide
  Adder adder_1 (
    .a({A7, A6, A5, A4, A3, A2, A1, A0}), .b({B7, B6, B5, B4, B3, B2, B1, B0}), .out(adder_1_out));  // open: cin, cout
  Subtractor subtractor_1 (
    .a({A7, A6, A5, A4, A3, A2, A1, A0}), .b({B7, B6, B5, B4, B3, B2, B1, B0}), .out(subtractor_1_out));  // open: bin, bout
  Multiplier multiplier_1 (
    .a({A7, A6, A5, A4, A3, A2, A1, A0}), .b({B7, B6, B5, B4, B3, B2, B1, B0}), .out(multiplier_1_out));  // open: cin, cout
  Divider divider_1 (
    .a({A7, A6, A5, A4, A3, A2, A1, A0}), .b({B7, B6, B5, B4, B3, B2, B1, B0}), .out(divider_1_out));  // open: upper, rem
  assign not_1_out = ~{A7, A6, A5, A4, A3, A2, A1, A0};  // NOT_Gate not_1, 8 bits wide
  Multiplexer #(.select(4), .width(8)) multiplexer_1 (
    .in0({A7, A6, A5, A4, A3, A2, A1, A0}), .in1(not_1_out), .in2(and_1_out), .in3(or_1_out),
    .in4(xor_1_out), .in5(nand_1_out), .in6(nor_1_out), .in7({8{1'b1}}), .in8({8{1'b0}}), .in9(adder_1_out),
    .in10(subtractor_1_out), .in11(multiplier_1_out), .in12(divider_1_out),
    .out({C7, C6, C5, C4, C3, C2, C1, C0}), .sel({O3, O2, O1, O0}));  // open: in13, in14, in15, en
endmodule
